# Fritzing sketch LEd_Digital_clock (saved by Fritzing 0.9.3b)
breadboards: 1

parts:
  Nano_V1 = Nano V3
  4_Digit_7_Segment_Display1 = 4 Digit 7 Segment Display
  KY-004_Button_Module1 = KY-004 Button Module
  KY-004_Button_Module2 = KY-004 Button Module
  YwRobot_Power_Supply2 = YwRobot Breadboard Power Supply [part_number=545043]

nets:
  N1: Nano_V1.GND, YwRobot_Power_Supply2.GND#13, YwRobot_Power_Supply2.GND#14
  N2: Nano_V1.D2, KY-004_Button_Module1.Vin
  N3: Nano_V1.D4, 4_Digit_7_Segment_Display1.DIO
  N4: Nano_V1.D5, 4_Digit_7_Segment_Display1.CLK
  VIN: Nano_V1.VIN, 4_Digit_7_Segment_Display1.VCC, YwRobot_Power_Supply2.VCC#9, YwRobot_Power_Supply2.VCC#10
  GND: 4_Digit_7_Segment_Display1.GND, KY-004_Button_Module1.-, KY-004_Button_Module2.Vin, YwRobot_Power_Supply2.GND#11, YwRobot_Power_Supply2.GND#12
  N5: YwRobot_Power_Supply2.VCC#5, YwRobot_Power_Supply2.VCC#6

custom parts:
  Nano V3: Can be used universally thanks to a compact design! By 14 digital in - and outputs and 6 analog inputs on the Nano V3 can also be used for larger projects! Thanks to the ATmega328 micro-controller, as well as more sophisticated programs to be executable! By Arduino compatibility in the Arduino IDE programmable! With FTDI Chip! Usual high quality and fast delivery directly from Germany by order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
  4 Digit 7 Segment Display: A module with 4 Digits divided into a 7-Segment display. The driver IC is TM1637. It can be used to display numbers, letters, etc. Details: 4 Digits red alpha-numeric display 8 adjustable light-Level Input voltage: 3.3~5.25 V DC Interface level can be 5V or 3.3 V
  KY-004 Button Module: Universal Button Module for direct use with Arduino, Raspberry & Co. Operating Voltage 3.3 V - 5 V Usual high quality and fast delivery directly from Germany by order AZ Delivery Of course, you will receive when you purchase through AZDelivery fully automatically and guarantees a Invoice incl. VAT and according to German Standards Guaranteed ROHS compliance by purchase from the German trader
  YwRobot Breadboard Power Supply: The YwRobot Breadboard Power Supply (MB-V2) has two power rails; they can be 5V or 3V3. Power to the module can be provided through the female USB socket or through the A10 (female) 2.1mm power jack.
