# Fritzing sketch LEd_Digital_clock_teil5 (saved by Fritzing 0.9.3b)
circuit board: 8.46667cm x 5.64444cm
breadboards: 3

parts:
  4_Digit_7_Segment_Display1 = 4 Digit 7 Segment Display
  KY-004_Button_Module1 = KY-004 Button Module
  KY-004_Button_Module2 = KY-004 Button Module
  YwRobot_Power_Supply2 = YwRobot Breadboard Power Supply [part_number=545043]  # not connected
  DHT-22_Temperature_and_humidity_sensor1 = DHT-22 Temperature and humidity sensor
  ZS-042_RTC1 = ZS-042 RTC Module  # not connected
  Bauteil2 = BH1750
  U1 = NodeMCU V1.0
  Bauteil3 = TXB0108 8-channel Bi-directional Logic Level Converter
  Nano_V2 = Nano V3

nets:
  N1: 4_Digit_7_Segment_Display1.CLK, Nano_V2.D4
  N2: 4_Digit_7_Segment_Display1.DIO, Nano_V2.D5
  VCC: 4_Digit_7_Segment_Display1.VCC, Bauteil2.VCC, Bauteil2.ADDR, U1.Vin, Bauteil3.VCCB, Nano_V2.5V
  GND: 4_Digit_7_Segment_Display1.GND, Bauteil2.GND, Bauteil3.GND, Nano_V2.GND
  VIN: KY-004_Button_Module1.Vin, KY-004_Button_Module2.Vin, DHT-22_Temperature_and_humidity_sensor1.GND, U1.GND
  N3: KY-004_Button_Module1.-, Nano_V2.D2
  N4: KY-004_Button_Module2.-, Nano_V2.D3
  N5: DHT-22_Temperature_and_humidity_sensor1.VCC, Bauteil3.OE, Bauteil3.VCCA
  N6: DHT-22_Temperature_and_humidity_sensor1.Data-signal, Bauteil3.A3
  N7: Bauteil2.SCL, Nano_V2.A5
  N8: Bauteil2.SDA, Nano_V2.A4
  N9: U1.RX, Bauteil3.A1
  N10: U1.TX, Bauteil3.A2
  N11: Bauteil3.B1, Nano_V2.D1/TX
  N12: Bauteil3.B2, Nano_V2.D0/RX
  N13: Bauteil3.B3, Nano_V2.D6

custom parts:
  4 Digit 7 Segment Display: A module with 4 Digits divided into a 7-Segment display. The driver IC is TM1637. It can be used to display numbers, letters, etc. Details: 4 Digits red alpha-numeric display 8 adjustable light-Level Input voltage: 3.3~5.25 V DC Interface level can be 5V or 3.3 V
  KY-004 Button Module: Universal Button Module for direct use with Arduino, Raspberry & Co. Operating Voltage 3.3 V - 5 V Usual high quality and fast delivery directly from Germany by order AZ Delivery Of course, you will receive when you purchase through AZDelivery fully automatically and guarantees a Invoice incl. VAT and according to German Standards Guaranteed ROHS compliance by purchase from the German trader
  YwRobot Breadboard Power Supply: The YwRobot Breadboard Power Supply (MB-V2) has two power rails; they can be 5V or 3V3. Power to the module can be provided through the female USB socket or through the A10 (female) 2.1mm power jack.
  DHT-22 Temperature and humidity sensor: A cost-effective digital Temperature- and Humidity sensor. By means of a capacitive humidity sensor and a Thermistor it measures the surrounding air and gives these values as a digital Signal on the data pin (no analog input pins needed). The Sensor is easy to use, but requires a precise timing to capture the data exactly. The measurement takes place every 2 sec. Details: Accuracy: 0.1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
  BH1750: Light Sensor
  NodeMCU V1.0: ESP8266 based NodeMCU
  TXB0108 8-channel Bi-directional Logic Level Converter: Because the Arduino (and Basic Stamp) are 5V devices, and most modern sensors, displays, flash cards and modes are 3.3V-only, many makers find that they need to perform level shifting/conversion to protect the 3.3V device from 5V. Although one can use resistors to make a divider, for high speed transfers, the resistors can add a lot of slew and cause havoc that is tough to debug. For that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
  Nano V3: Can be used universally thanks to a compact design! By 14 digital in - and outputs and 6 analog inputs on the Nano V3 can also be used for larger projects! Thanks to the ATmega328 micro-controller, as well as more sophisticated programs to be executable! By Arduino compatibility in the Arduino IDE programmable! With FTDI Chip! Usual high quality and fast delivery directly from Germany by order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
